# Fritzing sketch power-channel-p (saved by Fritzing 0.9.6b)
circuit board: 4.37052cm x 2.79463cm
breadboards: 1

parts:
  R1 = Resistor [tolerance=±5% resistance=150k package=THT]
  R2 = Resistor [tolerance=±5% resistance=680k package=THT]
  Q1 = Basic FET P-Channel [package="TO220 [THT]"]
  J1 = Screw terminal - 2 pins [package=THT]
  Q2 = NPN-Transistor [package="TO92 [THT]"]
  R3 = Resistor [tolerance=±5% resistance=150k package=THT]
  J2 = Screw terminal - 2 pins [package=THT]
  R4 = Resistor [tolerance=±5% resistance=150k package=THT]
  Q3 = NPN-Transistor [package="TO92 [THT]"]
  R5 = Resistor [tolerance=±5% resistance=10k package=THT]
  J3 = Screw terminal - 2 pins [package=THT]
  R6 = Resistor [tolerance=±5% resistance=10k package=THT]
  J4 = Screw terminal - 2 pins [package=THT]
  J5 = Screw terminal - 2 pins [package=THT]

nets:
  N1: R1.Pin_0, Q1.source, J1.pin1, J2.pin2
  N2: R1.Pin_1, R2.Pin_0, Q1.gate
  N3: R2.Pin_1, Q2.C
  N4: Q1.drain, J4.pin2
  N5: J1.pin2, Q2.E, Q3.E, J4.pin1, J5.pin2
  N6: Q2.B, R4.Pin_1, R6.Pin_0
  N7: R3.Pin_0, J2.pin1
  N8: R3.Pin_1, R4.Pin_0, Q3.C, J3.pin2
  N9: Q3.B, R5.Pin_0
  N10: R5.Pin_1, J3.pin1
  N11: R6.Pin_1, J5.pin1
